// Logisim project 8-Bit CPU V2.circ as structural Verilog
module ALU (
  input  [7:0] A,
  input  [7:0] B,
  input  [3:0] OP,
  input  ADC,
  input  CIN
);

  wire and_1_out, and_2_out, and_3_out, and_4_out, and_5_out, and_6_out, and_7_out, and_8_out, B_0_out,
       Cin_out, n1_bit_alu_2_c_out, n1_bit_alu_3_c_out, n1_bit_alu_4_c_out, n1_bit_alu_5_c_out,
       n1_bit_alu_6_c_out, n1_bit_alu_7_c_out, n1_bit_alu_8_c_out, nor_1_out, nor_2_out, nor_3_out,
       nor_4_out, nor_5_out, nor_6_out, nor_7_out, nor_8_out, SUB_out;

  // OR_Gate B_0 has open pins: out=B_0_out
  // OR_Gate SUB has open pins: out=SUB_out
  // OR_Gate Cin has open pins: out=Cin_out
  nor nor_1 (nor_1_out, SUB_out, B[7]);
  and and_1 (and_1_out, B_0_out, nor_1_out);
  nor nor_2 (nor_2_out, SUB_out, B[6]);
  and and_2 (and_2_out, B_0_out, nor_2_out);
  _1_Bit_ALU u_1_bit_alu_1 (.A(A[7]), .B(and_1_out), .C_in(n1_bit_alu_2_c_out));  // open: NOT, AND, OR, XOR, SUM, C_OUT
  nor nor_3 (nor_3_out, SUB_out, B[5]);
  and and_3 (and_3_out, B_0_out, nor_3_out);
  _1_Bit_ALU u_1_bit_alu_2 (
    .A(A[6]), .B(and_2_out), .C_in(n1_bit_alu_3_c_out), .C_OUT(n1_bit_alu_2_c_out));  // open: NOT, AND, OR, XOR, SUM
  nor nor_4 (nor_4_out, SUB_out, B[4]);
  and and_4 (and_4_out, B_0_out, nor_4_out);
  _1_Bit_ALU u_1_bit_alu_3 (
    .A(A[5]), .B(and_3_out), .C_in(n1_bit_alu_4_c_out), .C_OUT(n1_bit_alu_3_c_out));  // open: NOT, AND, OR, XOR, SUM
  nor nor_5 (nor_5_out, SUB_out, B[3]);
  and and_5 (and_5_out, B_0_out, nor_5_out);
  _1_Bit_ALU u_1_bit_alu_4 (
    .A(A[4]), .B(and_4_out), .C_in(n1_bit_alu_5_c_out), .C_OUT(n1_bit_alu_4_c_out));  // open: NOT, AND, OR, XOR, SUM
  nor nor_6 (nor_6_out, SUB_out, B[2]);
  and and_6 (and_6_out, B_0_out, nor_6_out);
  _1_Bit_ALU u_1_bit_alu_5 (
    .A(A[3]), .B(and_5_out), .C_in(n1_bit_alu_6_c_out), .C_OUT(n1_bit_alu_5_c_out));  // open: NOT, AND, OR, XOR, SUM
  nor nor_7 (nor_7_out, SUB_out, B[1]);
  and and_7 (and_7_out, B_0_out, nor_7_out);
  _1_Bit_ALU u_1_bit_alu_6 (
    .A(A[2]), .B(and_6_out), .C_in(n1_bit_alu_7_c_out), .C_OUT(n1_bit_alu_6_c_out));  // open: NOT, AND, OR, XOR, SUM
  nor nor_8 (nor_8_out, SUB_out, B[0]);
  and and_8 (and_8_out, B_0_out, nor_8_out);
  _1_Bit_ALU u_1_bit_alu_7 (
    .A(A[1]), .B(and_7_out), .C_in(n1_bit_alu_8_c_out), .C_OUT(n1_bit_alu_7_c_out));  // open: NOT, AND, OR, XOR, SUM
  _1_Bit_ALU u_1_bit_alu_8 (
    .A(A[0]), .B(and_8_out), .C_in(Cin_out), .C_OUT(n1_bit_alu_8_c_out));  // open: NOT, AND, OR, XOR, SUM
endmodule

module _1_Bit_ALU (
  input  A,
  input  B,
  input  C_in,
  output NOT,
  output AND,
  output OR,
  output XOR,
  output SUM,
  output C_OUT
);

  not not_1 (NOT, A);
  and and_1 (AND, A, B);
  or or_1 (OR, A, B);
  xor xor_1 (XOR, A, B);
  Adder #(.width(1)) adder_1 (.a(B), .b(A), .out(SUM), .cin(C_in), .cout(C_OUT));
endmodule
